# Fritzing sketch ultrasonicwaves_music_thai (saved by Fritzing 0.9.10b)

parts:
  부품1 = Arduino Uno (Rev3) - ICSP
  J1 = Piezo Speaker
  HC-SR04_Sensor_1 = HC-SR04 Ultrasonic Distance Sensor

nets:
  N1: 부품1.D8, HC-SR04_Sensor_1.TRIG
  N2: 부품1.D9_PWM, HC-SR04_Sensor_1.ECHO
  N3: 부품1.D10_PWM/SS, J1.pin1
  5V: 부품1.5V, HC-SR04_Sensor_1.VCC
  GND: 부품1.GND, J1.pin2, HC-SR04_Sensor_1.GND
